# Fritzing sketch line_follower (saved by Fritzing 0.9.10b)
circuit board: 9.26781cm x 5.31124cm
circuit board: 4.59272cm x 7.93471cm

parts:
  Part1 = Arduino Nano (Rev3.0)
  Voltage_regulator = Voltage Regulator [package=to220-igo]
  Battery = BC9VPC [package=bc9vpc]
  Motor_driver = L293D [package=THT]
  Cell = LIPO-2000mAh [package=lipo-2000]
  Motor_left = DC Motor [voltage_(max)=6V voltage_(min)=3V]
  Motor_right = DC Motor [voltage_(max)=6V voltage_(min)=3V]
  left_1 = TCRT5000 [package=THT]
  right_2 = TCRT5000 [package=THT]
  center = TCRT5000 [package=THT]
  left_2 = TCRT5000 [package=THT]
  right_1 = TCRT5000 [package=THT]
  R_c_gnd = Resistor [tolerance=±1% resistance=4.7k power=0.25 package=THT]
  R_l1_gnd = Resistor [tolerance=±10% resistance=22k power=0.25 package=THT]
  R_l2_gnd = Resistor [tolerance=±10% resistance=4.7k power=0.25 package=THT]
  R_r1_gnd = Resistor [tolerance=±10% resistance=6.8k power=0.25 package=THT]
  R_r2_vcc = Resistor [tolerance=±5% resistance=100 power=0.25 package=THT]
  R_r2_gnd = Resistor [tolerance=±10% resistance=4.7k power=0.25 package=THT]
  R_r1_vcc = Resistor [tolerance=±20% resistance=100 power=0.25 package=THT]
  R_l1_vcc = Resistor [tolerance=±20% resistance=100 power=0.25 package=THT]
  R_c_vcc = Resistor [tolerance=±20% resistance=100 power=0.25 package=THT]
  R_l2_vcc = Resistor [tolerance=±20% resistance=100 power=0.25 package=THT]
  S1 = SWITCH-DPDT [package=ms]
  Power_plug1 = Power plug

nets:
  GND: Part1.GND, Voltage_regulator.GND, Battery.V-, Motor_driver.0V, Cell.-, left_1.Pin_3, right_2.Pin_3, center.Pin_3, left_2.Pin_3, right_1.Pin_3, R_c_gnd.Pin_0, R_l1_gnd.Pin_0, R_l2_gnd.Pin_0, R_r1_gnd.Pin_0, R_r2_gnd.Pin_1, Power_plug1.GND
  N1: Part1.D3, Motor_driver.In_3
  N2: Part1.D5, Motor_driver.In_4
  N3: Part1.D6, Motor_driver.In_2
  N4: Part1.D9, Motor_driver.In_1
  N5: Part1.VIN, Voltage_regulator.OUT, Motor_driver.Enable_1, Motor_driver.Enable_2, Motor_driver.+V, left_1.Pin_1, right_2.Pin_1, center.Pin_1, left_2.Pin_1, right_1.Pin_1, R_r2_vcc.Pin_0, R_r1_vcc.Pin_0, R_l1_vcc.Pin_0, R_c_vcc.Pin_0, R_l2_vcc.Pin_0
  N6: Part1.A7, right_2.Pin_2, R_r2_gnd.Pin_0
  N7: Part1.A6, right_1.Pin_2, R_r1_gnd.Pin_1
  N8: Part1.A2, center.Pin_2, R_c_gnd.Pin_1
  N9: Part1.A1, left_1.Pin_2, R_l1_gnd.Pin_1
  N10: Part1.A0, left_2.Pin_2, R_l2_gnd.Pin_1
  N11: Voltage_regulator.IN, Battery.V+, S1.2, S1.3
  N12: Motor_driver.Out_1_(_Controlled_by_Enable_1_), Motor_right.pin_2
  N13: Motor_driver.Out_2_(_Controlled_by_Enable_1_), Motor_right.pin_1
  N14: Motor_driver.+Vmotor, Cell.+, S1.5, S1.6, Power_plug1.VCC
  N15: Motor_driver.Out_3_(_Controlled_by_Enable_2_), Motor_left.pin_2
  N16: Motor_driver.Out_4_(_Controlled_by_Enable_2_), Motor_left.pin_1
  N17: left_1.Pin_4, R_l1_vcc.Pin_1
  N18: right_2.Pin_4, R_r2_vcc.Pin_1
  N19: center.Pin_4, R_c_vcc.Pin_1
  N20: left_2.Pin_4, R_l2_vcc.Pin_1
  N21: right_1.Pin_4, R_r1_vcc.Pin_1

custom parts:
  TCRT5000: TCRT5000 optical reflective sensor
